# Fritzing sketch smartRoomControllerFritzing (saved by Fritzing 0.9.9b)
breadboards: 1

parts:
  Teensy_3_1 = Teensy 3.1  # not connected
  S1 = Pushbutton [package="[THT]"]
  R1 = Resistor [tolerance=±5% power=0.25 resistance=220 package=THT]
  Part1 = 12 NeoPixel Ring [part_number=1643]
  OLED_I2C1 = OLED 128x64 I2C Monochrome Display
  Part2 = Passive Buzzer
  PIR1 = PIR sensor
  WIZ820io1 = WIZ820io [part_number=WIZ820io]

nets:
  N1: S1.Pin_1, S1.Pin_2, R1.Pin_0
  VDD: S1.Pin_3, S1.Pin_4, Part1.VDD, OLED_I2C1.VDD, Part2.S, PIR1.VDD, WIZ820io1.VIN
  GND: R1.Pin_1, Part1.GND, OLED_I2C1.GND, Part2.GND, PIR1.GND, WIZ820io1.GND

custom parts:
  Pushbutton: A generic pushbutton.
  12 NeoPixel Ring: 12 ultra bright smart LED NeoPixels are arranged in a circle with 1.5" (37mm) outer diameter. The rings are 'chainable' - connect the output pin of one to the input pin of another. Use only one microcontroller pin to control as many as you can chain together! Each LED is addressable as the driver chip is inside the LED. Each one has ~18mA constant current drive so the color will be very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
